# Fritzing sketch MSGEQ7 (saved by Fritzing 0.7.10b)
breadboards: 1

parts:
  U1 = LM386 [package=dip08]
  R2 = Resistor [tolerance=±5% resistance=100 package=THT]
  R4 = Resistor [tolerance=±5% resistance=100 package=THT]
  10kΩ_Pot_=_Mic_Volume = Rotary Potentiometer (Small) [maximum_resistance=100kΩ]
  MIC1 = Microphone
  10μF = Electrolytic Capacitor [package=THT]
  100kΩ_Pot_=_Sensitivity = Rotary Potentiometer (Small) [maximum_resistance=100kΩ]
  10μF_2 = Electrolytic Capacitor [package=THT]
  0_1uf = Ceramic Capacitor [package=THT]
  1μF = Tantalum Capacitor [capacitance="1 μF" package="D 7343 [SMD, tantalum]"]
  1μF_2 = Tantalum Capacitor [capacitance="1 μF" package="D 7343 [SMD, tantalum]"]
  R7 = Resistor [tolerance=±5% resistance=200 package=THT]
  33pF = Ceramic Disk Capacitor [package=THT]
  IC3 = IC, DIP package, 8 pins [chip_label=MSGEQ7]
  J1 = Generic female header - 5 pins [package=THT]
  0_1μF = Ceramic Capacitor [package=THT]
  0_1μF_2 = Ceramic Capacitor [package=THT]

nets:
  N1: U1.GAIN, 10μF_2.+
  N2: U1.-IN, U1.V-, R2.Pin_1, MIC1.pin1, 10μF_2.-, 0_1uf.pin_1, 33pF.pin_0, IC3.pin2, J1.pin5
  N3: U1.+IN, 1μF_2.-
  N4: U1.OUT, 10μF.-, 1μF.-
  N5: R2.Pin_0, 1μF.+
  N6: R4.Pin_0, MIC1.pin2, 1μF_2.+
  N7: R4.Pin_1, 10kΩ_Pot_=_Mic_Volume.wiper, 10kΩ_Pot_=_Mic_Volume.leg2
  N8: 10kΩ_Pot_=_Mic_Volume.leg1, 0_1uf.pin_0, R7.Pin_0, IC3.pin1, J1.pin2, 0_1μF.pin_1
  N9: 10μF.+, 100kΩ_Pot_=_Sensitivity.leg1
  N10: 100kΩ_Pot_=_Sensitivity.leg2, 0_1μF_2.pin_0
  N11: R7.Pin_1, 33pF.pin_1, IC3.pin8
  N12: IC3.pin3, J1.pin1
  N13: IC3.pin4, J1.pin4
  N14: IC3.pin5, 0_1μF_2.pin_1
  N15: IC3.pin6, 0_1μF.pin_0
  N16: IC3.pin7, J1.pin3
